# Fritzing sketch sketch (saved by Fritzing 0.9.9b)
breadboards: 1

parts:
  U1 = Module 4 Relais 5V [package="Module 4 Relais 5V"]
  M1 = ESP32 FIREBEETLE IOT V3 [part_number=ESP32_FIREBEETLE]
  Power_plug1 = Power plug
  Power_plug2 = Power plug
  J5 = Camdenboss CTB0158-2 [part_number=CTB0158-2 package=THT]
  J6 = Camdenboss CTB0158-2 [part_number=CTB0158-2 package=THT]
  J7 = Camdenboss CTB0158-3 [part_number=CTB0158-3 package=THT]

nets:
  GND: U1.GND, M1.GND
  N1: U1.IN3, M1.IO25/D2
  N2: U1.IN4, M1.IO26/D3
  N3: U1.K3-NF, U1.K4-NF, Power_plug2.GND
  N4: U1.K3-NO, J6.terminal_2
  N5: U1.K4-NO, J5.terminal_2
  VCC: M1.VCC, Power_plug1.VCC
  N6: Power_plug2.VCC, J7.terminal_1
  N7: J5.terminal_1, J7.terminal_2
  N8: J6.terminal_1, J7.terminal_3

notes:
  +5V Power Supply
  AC~ 220V
  FAN01
  FAN02

custom parts:
  Module 4 Relais 5V: Module 4 Relais 5V 4x SPD-06VDC-SD-C
  ESP32 FIREBEETLE IOT V3: DFRobot Firebeetle ESP32 IOT Microcontroller V3, 36-Pin ESP32.
